# Fritzing sketch gyro HID Sketch (saved by Fritzing 0.9.4)

parts:
  Part2 = Adafruit Feather nRF52840 [part_number=4062]
  Part3 = TRRS 3.5mm Jack Breakout
  Part4 = TRRS 3.5mm Jack Breakout
  Part5 = TRRS 3.5mm Jack Breakout
  Part6 = TRRS 3.5mm Jack Breakout
  Part7 = TRRS 3.5mm Jack Breakout
  J1 = Camdenboss CTB0158-7 [part_number=CTB0158-7 package=THT]
  Part8 = Adafruit LSM6DS33 6-DoF Accel + Gyro IMU [part_number="Adafruit #4480"]  # not connected

nets:
  N1: Part2.3.3V, Part7.TIP
  N2: Part2.GND, J1.terminal_2
  N3: Part2.A1, Part3.TIP
  N4: Part2.A2, Part4.TIP
  N5: Part2.A3, Part5.TIP
  N6: Part2.SDA, Part7.RING1
  N7: Part2.SCL, Part7.RING2
  N8: Part3.SLEEVE, J1.terminal_3
  N9: Part4.SLEEVE, J1.terminal_4
  N10: Part5.SLEEVE, J1.terminal_5
  N11: Part6.SLEEVE, J1.terminal_6
  N12: Part7.SLEEVE, J1.terminal_7

notes:
  left
  button
  right
  button
  scroll
  button
  dwell
  toggle
  button
  gyro
  I2C
  IMU
  connect all grounds together. This can use a terminal block or simply twist them together and secure.
  Connect Stemma / Qwiic / JST sh connector to 3.5mm jack cable. See assembly manual for detailed instructions. Yellow SCL, Blue SDA, Red VCC, Black GND.

custom parts:
  Adafruit Feather nRF52840: The Adafruit Feather nRF52840 Express is our take on an 'all-in-one' Arduino-compatible + Bluetooth Low Energy with built in USB plus battery charging, 1 MB of FLASH and 256KB of SRAM. With native USB it's even ready to join the CircuitPython party. For this chip, we've added Arduino IDE support - you can program the nRF52840 chip directly to take full advantage of the Cortex-M4 processor, and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
  Adafruit LSM6DS33 6-DoF Accel + Gyro IMU: Add motion and orientation sensing to your Arduino project with this affordable 6 Degree of Freedom (6-DoF) sensor with sensors from ST. The board includes an LSM6DS33, a 6-DoF IMU accelerometer + gyro. The 3-axis accelerometer, can tell you which direction is down towards the Earth (by measuring gravity) or how fast the board is accelerating in 3D space. The 3-axis gyroscope that can measure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
